// Logisim project exercicio1.circ as structural Verilog: 1 circuit, main circuit main
module main (
  input  in_1,
  input  in_2
);

  wire transistor_1_out, transistor_2_out, transistor_3_out;

  Transistor transistor_1 (.in(1'b1), .out(transistor_1_out), .gate(in_1));
  Transistor #(.\type ("n")) transistor_2 (.in(transistor_1_out), .out(transistor_2_out), .gate(in_1));
  Transistor #(.\type ("n")) transistor_3 (.in(transistor_2_out), .out(transistor_3_out), .gate(in_2));
  Transistor transistor_4 (.in(1'b1), .out(transistor_1_out), .gate(in_2));
  LED led_1 (.in(transistor_1_out));
  // also tied to GND on the sheet: transistor_3_out
endmodule
