// Logisim project exercicio2.circ as structural Verilog: 1 circuit, main circuit main
module main (
  input  A0,
  input  A3,
  input  A1,
  input  A4,
  input  B1,
  input  B4,
  input  A2,
  input  A5,
  input  B2,
  input  B5
);

  wire nand_1_out, nand_2_out, nand_3_out, nand_4_out, nand_5_out, nand_6_out, nor_1_out, nor_2_out,
       nor_3_out, nor_4_out, nor_5_out, nor_6_out;

  nand nand_1 (nand_1_out, A1, B1);
  nand nand_2 (nand_2_out, A2, A2);
  nand nand_3 (nand_3_out, B2, B2);
  nand nand_4 (nand_4_out, A0, A0);
  LED A0_neg (.in(nand_4_out));
  nand nand_5 (nand_5_out, nand_1_out, nand_1_out);
  LED A1_E_B1 (.in(nand_5_out));
  nand nand_6 (nand_6_out, nand_2_out, nand_3_out);
  LED A2_OU_B2 (.in(nand_6_out));
  nor nor_1 (nor_1_out, A4, B4);
  nor nor_2 (nor_2_out, A5, A5);
  nor nor_3 (nor_3_out, B5, B5);
  nor nor_4 (nor_4_out, A3, A3);
  LED A3_neg (.in(nor_4_out));
  nor nor_5 (nor_5_out, nor_1_out, nor_1_out);
  LED A4_OU_B4 (.in(nor_5_out));
  nor nor_6 (nor_6_out, nor_2_out, nor_3_out);
  LED A5_E_B5 (.in(nor_6_out));
endmodule
