// Logisim project Automato_Reconhecer_Par_Zeros.circ as structural Verilog: 1 circuit, main circuit main
module main (
  input  in_1,
  input  in_2,
  input  in_3,
  input  in_4,
  input  in_5,
  input  in_6,
  input  in_7,
  input  in_8,
  input  Carrega,
  input  Opera,
  input  in_11,
  output out_12
);

  wire and_1_out, and_2_out, and_3_out, and_4_out, clock_1_out, d_ff_1_q, d_ff_1_qn, d_ff_2_q, d_ff_2_qn,
       not_1_out, or_1_out, or_2_out;

  Clock clock_1 (.out(clock_1_out));
  Shift_Register shift_register_1 (
    .shift(Opera), .clk(clock_1_out), .out(out_12), .load(Carrega), .d0(in_1), .d1(in_2), .d2(in_3),
    .d3(in_4), .d4(in_5), .d5(in_6), .d6(in_7), .d7(in_8));  // open: in, clr, q0, q1, q2, q3, q4, q5, q6, q7
  D_Flip_Flop d_ff_1 (
    .clk(clock_1_out), .D(or_2_out), .Q(d_ff_1_q), .Qn(d_ff_1_qn), .preset(in_11), .en(Opera));  // open: reset
  D_Flip_Flop d_ff_2 (
    .clk(clock_1_out), .D(or_1_out), .Q(d_ff_2_q), .Qn(d_ff_2_qn), .en(Opera), .reset(in_11));  // open: preset
  not not_1 (not_1_out, out_12);
  and and_1 (and_1_out, not_1_out, d_ff_1_q, d_ff_2_qn);
  and and_2 (and_2_out, out_12, d_ff_1_qn, d_ff_2_q);
  or or_1 (or_1_out, and_1_out, and_2_out);
  and and_3 (and_3_out, out_12, d_ff_1_q, d_ff_2_qn);
  and and_4 (and_4_out, not_1_out, d_ff_1_qn, d_ff_2_q);
  or or_2 (or_2_out, and_4_out, and_3_out);
  LED led_1 (.in(d_ff_1_q));

  // Notes on the sheet:
  //   Põe no estado inicial
  //   Estado=1
  //   Estado=2
  //   Entrada: o que carregar e serializar
  //   Saída do deslocador: entrada serializada
  //   Também é a entrada do autômato
  //   Aceita
endmodule
