// Logisim project Automatos.circ as structural Verilog: 1 circuit, main circuit main
module main (
);

  wire adder_1_cout, and_1_out, clock_1_out, d_ff_1_q, d_ff_1_qn, nor_1_out, not_1_out, or_1_out, undriven,
       undriven_2, undriven_3, undriven_4, undriven_5, undriven_6, undriven_7, undriven_8, undriven_9;
  wire [3:0] register_1_q, register_1_q_2;
  wire [7:0] adder_1_out;

  not not_1 (not_1_out, undriven);
  Clock clock_1 (.out(clock_1_out));
  Hex_Digit_Display hex_digit_display_1 (.value(register_1_q));  // open: dp
  Hex_Digit_Display hex_digit_display_2 (.value(register_1_q_2));  // open: dp
  Register register_1 (.D(adder_1_out), .Q({register_1_q_2, register_1_q}), .clk(clock_1_out));  // open: en, clr
  and and_1 (and_1_out, undriven_2, undriven_3);
  Adder adder_1 (.a({register_1_q_2, register_1_q}), .b(8'h2a), .out(adder_1_out), .cout(adder_1_cout));  // open: cin
  LED led_1 (.in(adder_1_cout));
  or or_1 (or_1_out, undriven_4, undriven_5);
  nor nor_1 (nor_1_out, undriven_6, undriven_7);
  D_Flip_Flop d_ff_1 (.clk(undriven_8), .D(undriven_9), .Q(d_ff_1_q), .Qn(d_ff_1_qn));  // open: preset, en, reset

  // Notes on the sheet:
  //   A
  //   porta NOT - S=NOT(A)
  //   S
  //   clock
  //   Entrada de 8 bits
  //   A
  //   B
  //   displays: mostram o estado
  //   registrador de 8 bits
  //   porta E - S=AB
  //   somador de 8 bits
  //   este circuito implementa um autômato. O registrador armazena o estado, o somador calcula o próximo estado.
  //   a) enuncie o que o autômato faz - quanto mais próximo da descrição de um comando de um processador, melhor a explicação.
  //   A
  //   S
  //   B
  //   LED indicador de vai um
  //   b-) deseja-se que o autômato pare antes que o estado seja atualizado com um transbordamento (overflow). O que precisa ser ajustado no circuito? Desenhe um novo circuito.
  //   porta OU - S=A+B
  //   S
  //   A
  //   B
  //   porta NOU - S=NOT(A+B)
  //   S
  //   clock
  //   D
  //   Flip-Flop tipo D
  //   Q
  //   NOT(Q)
endmodule
