// Logisim project Contador_3_bits.circ as structural Verilog: 1 circuit, main circuit main
module main (
);

  wire and_1_out, and_2_out, and_3_out, and_4_out, clock_1_out, clock_2_out, d_ff_1_q, d_ff_1_qn, d_ff_2_q,
       d_ff_2_qn, d_ff_3_q, d_ff_3_qn, or_1_out, xor_1_out;
  wire [2:0] counter_1_q;

  Clock clock_1 (.out(clock_1_out));
  D_Flip_Flop d_ff_1 (.clk(clock_1_out), .D(or_1_out), .Q(d_ff_1_q), .Qn(d_ff_1_qn));  // open: preset, en, reset
  D_Flip_Flop d_ff_2 (.clk(clock_1_out), .D(xor_1_out), .Q(d_ff_2_q), .Qn(d_ff_2_qn));  // open: preset, en, reset
  D_Flip_Flop d_ff_3 (.clk(clock_1_out), .D(d_ff_3_qn), .Q(d_ff_3_q), .Qn(d_ff_3_qn));  // open: preset, en, reset
  xor xor_1 (xor_1_out, d_ff_3_q, d_ff_2_q);
  and and_1 (and_1_out, d_ff_1_qn, d_ff_2_q, d_ff_3_q);
  and and_2 (and_2_out, d_ff_1_q, d_ff_2_qn, d_ff_3_qn);
  or or_1 (or_1_out, and_1_out, and_2_out, and_4_out, and_3_out);
  and and_3 (and_3_out, d_ff_1_q, d_ff_2_q, d_ff_3_qn);
  and and_4 (and_4_out, d_ff_1_q, d_ff_2_qn, d_ff_3_q);
  LED led_1 (.in(d_ff_1_q));
  LED led_2 (.in(d_ff_2_q));
  LED led_3 (.in(d_ff_3_q));
  Clock clock_2 (.out(clock_2_out));
  Counter #(.width(3), .max('h7)) counter_1 (.Q(counter_1_q), .clk(clock_2_out));  // open: load, D, count, carry, clr
  LED led_4 (.in(counter_1_q[2]));
  LED led_5 (.in(counter_1_q[1]));
  LED led_6 (.in(counter_1_q[0]));

  // Notes on the sheet:
  //   Q2
  //   Q1
  //   Q0
endmodule
