// Logisim project contador.circ as structural Verilog: 1 circuit, main circuit main
module main (
);

  wire clock_1_out;
  wire [7:0] counter_1_q, ram_1_data;

  Clock clock_1 (.out(clock_1_out));
  Counter counter_1 (.Q(counter_1_q), .clk(clock_1_out));  // open: load, D, count, carry, clr
  RAM ram_1 (.addr(counter_1_q), .data(ram_1_data), .clk(clock_1_out));  // open: sel, ld, clr
  Hex_Digit_Display hex_digit_display_1 (.value(ram_1_data[3:0]));  // open: dp
  Hex_Digit_Display hex_digit_display_2 (.value(ram_1_data[7:4]));  // open: dp
endmodule
